# Fritzing sketch Pico 7 segment reordered bits (saved by Fritzing 0.9.6b)
breadboards: 1

parts:
  Mod1 = Raspberry Pi Pico
  Q1 = NPN-Transistor [package="TO92 [THT]"]
  R1 = Resistor [tolerance=±5% power=0.25 resistance=220 package=THT]
  R2 = Resistor [tolerance=±5% power=0.25 resistance=220 package=THT]
  Q2 = NPN-Transistor [package="TO92 [THT]"]
  Q3 = NPN-Transistor [package="TO92 [THT]"]
  Q4 = NPN-Transistor [package="TO92 [THT]"]
  Q5 = NPN-Transistor [package="TO92 [THT]"]
  Q6 = NPN-Transistor [package="TO92 [THT]"]
  Q7 = NPN-Transistor [package="TO92 [THT]"]
  Q8 = NPN-Transistor [package="TO92 [THT]"]
  Q9 = PNP-Transistor [package="TO92 [THT]"]
  Q10 = PNP-Transistor [package="TO92 [THT]"]
  Q11 = PNP-Transistor [package="TO92 [THT]"]
  Q12 = PNP-Transistor [package="TO92 [THT]"]
  R3 = Resistor [tolerance=±5% power=0.25 resistance=220 package=THT]
  R4 = Resistor [tolerance=±5% power=0.25 resistance=220 package=THT]
  R5 = Resistor [tolerance=±5% power=0.25 resistance=220 package=THT]
  R6 = Resistor [tolerance=±5% power=0.25 resistance=220 package=THT]
  R7 = Resistor [tolerance=±5% power=0.25 resistance=220 package=THT]
  R8 = Resistor [tolerance=±5% power=0.25 resistance=220 package=THT]
  R9 = Resistor [tolerance=±5% power=0.25 resistance=220 package=THT]
  R10 = Resistor [tolerance=±5% power=0.25 resistance=220 package=THT]
  R11 = Resistor [tolerance=±5% power=0.25 resistance=220 package=THT]
  R12 = Resistor [tolerance=±5% power=0.25 resistance=220 package=THT]
  R13 = Resistor [tolerance=±5% power=0.25 resistance=220 package=THT]
  R14 = Resistor [tolerance=±5% power=0.25 resistance=220 package=THT]
  R15 = Resistor [tolerance=±5% power=0.25 resistance=220 package=THT]
  R16 = Resistor [tolerance=±5% power=0.25 resistance=220 package=THT]
  R18 = Resistor [tolerance=±5% power=0.25 resistance=220 package=THT]
  R19 = Resistor [tolerance=±5% power=0.25 resistance=220 package=THT]
  R20 = Resistor [tolerance=±5% power=0.25 resistance=220 package=THT]
  R21 = Resistor [tolerance=±5% power=0.25 resistance=220 package=THT]
  LED2 = 7-SEGMENT-4DIGIT-YOUNGSUN [package=7-segment-4digit-youngsun-longpads]

nets:
  N1: Mod1.pin_3, Mod1.pin_8, Mod1.pin_13, Mod1.pin_18, Mod1.pin_23, Mod1.pin_28, Mod1.pin_33, Mod1.pin_38, Q1.E, Q2.E, Q3.E, Q4.E, Q5.E, Q6.E, Q7.E, Q8.E
  N2: Mod1.pin_11, R15.Pin_0
  N3: Mod1.pin_12, R13.Pin_0
  N4: Mod1.pin_14, R11.Pin_0
  N5: Mod1.pin_15, R9.Pin_0
  N6: Mod1.pin_16, R6.Pin_0
  N7: Mod1.pin_17, R5.Pin_0
  N8: Mod1.pin_19, R3.Pin_0
  N9: Mod1.pin_20, R1.Pin_0
  N10: Mod1.pin_21, R21.Pin_1
  N11: Mod1.pin_22, R20.Pin_1
  N12: Mod1.pin_24, R19.Pin_1
  N13: Mod1.pin_25, R18.Pin_1
  N14: Mod1.pin_36, Q9.E, Q10.E, Q11.E, Q12.E
  N15: Q1.B, R1.Pin_1
  N16: Q1.C, R2.Pin_1
  N17: R2.Pin_0, LED2.A
  N18: Q2.B, R3.Pin_1
  N19: Q2.C, R4.Pin_1
  N20: Q3.B, R5.Pin_1
  N21: Q3.C, R7.Pin_1
  N22: Q4.B, R6.Pin_1
  N23: Q4.C, R8.Pin_1
  N24: Q5.B, R9.Pin_1
  N25: Q5.C, R10.Pin_1
  N26: Q6.B, R11.Pin_1
  N27: Q6.C, R12.Pin_1
  N28: Q7.B, R13.Pin_1
  N29: Q7.C, R14.Pin_1
  N30: Q8.B, R15.Pin_1
  N31: Q8.C, R16.Pin_1
  N32: Q9.B, R20.Pin_0
  N33: Q9.C, LED2.DIG2
  N34: Q10.B, R19.Pin_0
  N35: Q10.C, LED2.DIG3
  N36: Q11.B, R21.Pin_0
  N37: Q11.C, LED2.DIG1
  N38: Q12.B, R18.Pin_0
  N39: Q12.C, LED2.DIG4
  N40: R4.Pin_0, LED2.B
  N41: R7.Pin_0, LED2.C
  N42: R8.Pin_0, LED2.D
  N43: R10.Pin_0, LED2.E
  N44: R12.Pin_0, LED2.F
  N45: R14.Pin_0, LED2.G
  N46: R16.Pin_0, LED2.DP

custom parts:
  Raspberry Pi Pico: Raspberry Pi Pico. Based around the RP2040 microcontroller the Pico is a low cost microcontroller device bringing Raspberry Pi quality, cost, and easy of use to the microcontroller space. Jan 2021, Split part in to two versions: tht (this one) and SMD. This one will drill holes for a .1 in header in pcb to allow plugging in the module as well as providing pads to solder the module to the top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
  7-SEGMENT-4DIGIT-YOUNGSUN: This is a part for the 4-Digit 7-segment LEDs from Young Sun. Different from the Digikey LEDs, all 16 pins are used. The LONGPADS Variant is used for a test jig, but you may like it because there is more pad to solder to. If you are concerned about routing space, the standard works just fine though.
